# Fritzing sketch Rascar (saved by Fritzing 0.9.3b)

parts:
  Raspberry_Pi_1 = Raspberry Pi 3 [part_number=RPI-3-V1.2]
  S1 = H-Bridge with L298N
  M1 = Getriebemotor
  M2 = Getriebemotor
  M3 = Getriebemotor  # not connected
  M4 = Getriebemotor
  VCC2 = Battery block 9V

nets:
  N1: Raspberry_Pi_1.GIPO17, S1.ENA
  N2: Raspberry_Pi_1.GIPO27, S1.ENB
  N3: Raspberry_Pi_1.GIPO24, S1.IN4
  N4: Raspberry_Pi_1.GIPO23, S1.IN3
  N5: Raspberry_Pi_1.GIPO15, S1.IN2
  N6: Raspberry_Pi_1.GIPO14, S1.IN1
  GND: Raspberry_Pi_1.GND, S1.GND
  5V: Raspberry_Pi_1.5V, S1.12V, VCC2.+
  N7: S1.M1-01, M1.pin_1
  N8: S1.M2-01, M4.pin_1
  N9: S1.M2-02, M2.pin_1

custom parts:
  H-Bridge with L298N: h-bridge
